# Fritzing sketch Raspberry-Pi+MAX31850-Thermocouple-Amplifier (saved by Fritzing 0.9.2b)
breadboards: 1

parts:
  BREAKOUT1 = MAX31850 Thermocouple Breakout
  R1 = Resistor [tolerance=±5% resistance=4.7 package=THT]
  Raspberry_Pi1 = Raspberry Pi 2

nets:
  GND: BREAKOUT1.GND, Raspberry_Pi1.GND
  VIN: BREAKOUT1.VIN, R1.Pin_1, Raspberry_Pi1.3v3
  N1: BREAKOUT1.DATA, R1.Pin_0, Raspberry_Pi1.GPIO4
